# Fritzing sketch scheme (saved by Fritzing 0.9.10b)

parts:
  Компонент1 = Arduino Uno (Rev3) - ICSP
  Компонент2 = 16-Channel 12-bit PWM Servo Driver - I2C [part_number=815]
  Компонент3 = 16-Channel 12-bit PWM Servo Driver - I2C [part_number=815]
  SERVO1 = Tower Pro SG90 servo [part_number=101246]  # not connected
  SERVO2 = Tower Pro SG90 servo [part_number=101246]  # not connected
  SERVO3 = Tower Pro SG90 servo [part_number=101246]  # not connected
  SERVO4 = Tower Pro SG90 servo [part_number=101246]  # not connected
  SERVO5 = Tower Pro SG90 servo [part_number=101246]  # not connected
  SERVO6 = Tower Pro SG90 servo [part_number=101246]  # not connected
  SERVO7 = Tower Pro SG90 servo [part_number=101246]  # not connected
  SERVO8 = Tower Pro SG90 servo [part_number=101246]  # not connected
  SERVO9 = Tower Pro SG90 servo [part_number=101246]  # not connected
  SERVO10 = Tower Pro SG90 servo [part_number=101246]  # not connected
  SERVO11 = Tower Pro SG90 servo [part_number=101246]  # not connected
  SERVO12 = Tower Pro SG90 servo [part_number=101246]  # not connected
  SERVO13 = Tower Pro SG90 servo [part_number=101246]  # not connected
  SERVO14 = Tower Pro SG90 servo [part_number=101246]  # not connected
  SERVO15 = Tower Pro SG90 servo [part_number=101246]  # not connected
  SERVO16 = Tower Pro SG90 servo [part_number=101246]  # not connected
  SERVO17 = Tower Pro SG90 servo [part_number=101246]  # not connected
  Power_plug1 = Power plug
  Компонент5 = 16-Channel 12-bit PWM Servo Driver - I2C [part_number=815]
  Компонент6 = 16-Channel 12-bit PWM Servo Driver - I2C [part_number=815]
  Power_plug2 = Power plug  # not connected
  Компонент7 = Arduino Nano (Rev3.0)

nets:
  N1: Компонент1.A4/SDA, Компонент2.SDA, Компонент3.SDA
  N2: Компонент1.A5/SCL, Компонент2.SCL, Компонент3.SCL
  GND: Компонент1.GND, Компонент2.GND, Компонент3.GND, Power_plug1.GND
  VCC: Компонент1.5V, Компонент2.VCC, Компонент3.VCC
  N3: Компонент2.PWRIN, Power_plug1.VCC
  N4: Компонент2.5.0V, Компонент3.5.0V
  N5: Компонент2.OE, Компонент3.OE
  VCC_2: Компонент5.VCC, Компонент6.VCC, Компонент7.5V
  N6: Компонент5.SDA, Компонент6.SDA, Компонент7.A4
  N7: Компонент5.SCL, Компонент6.SCL, Компонент7.A5
  GND_2: Компонент5.GND, Компонент6.GND, Компонент7.GND
  N8: Компонент5.5.0V, Компонент6.5.0V
  N9: Компонент5.OE, Компонент6.OE

custom parts:
  16-Channel 12-bit PWM Servo Driver - I2C: You want to make a cool robot, maybe a hexapod walker, or maybe just a piece of art with a lot of moving parts. Or maybe you want to drive a lot of LEDs with precise PWM output. Using only two pins, control 16 free-running PWM outputs! You can even chain up 62 breakouts to control up to 992 PWM outputs.
  Tower Pro SG90 servo: Original file by John De Cristofaro http://www.adafruit.com/products/1449 Adafruit Feedback Servo (Small) Edited by: e-radionica.com 28/9/2015
